// Logisim project jrmips.circ as structural Verilog: 5 circuits, main circuit main
module main (
);

  wire ALU_A, Clk, Halt, MemRead, MemWrite, not_1_out, Put, S_Ext, SubOp, W_En1, W_En2;
  wire [1:0] ALU_B, PC, Write1;
  wire [2:0] Rs, Rs_1;
  wire [3:0] ALU, OpCode;
  wire [7:0] Imm, multiplexer_1_out, multiplexer_2_out, PC_1, PC_q;
  wire [15:0] ALU_Result, Extend, Mem_Data, multiplexer_3_out, multiplexer_4_out, multiplexer_5_out, R_Data1,
       regfile_1_read_data2, register_1_q, Upper_Bits;

  Multiplexer #(.width(8), .enable("false")) multiplexer_1 (
    .in0(PC_1), .in1(Imm), .out(multiplexer_1_out), .sel(ALU_Result[0]));
  Adder #(.width(3)) adder_1 (.a(Rs), .b(3'b001), .out(Rs_1));  // open: cin, cout
  Multiplexer #(.select(2), .width(8), .enable("false")) multiplexer_2 (
    .in0(PC_1), .in1(multiplexer_1_out), .in2(Imm), .in3(R_Data1[7:0]), .out(multiplexer_2_out), .sel(PC));
  Multiplexer #(.select(2), .width(16), .enable("false")) multiplexer_3 (
    .in0(ALU_Result), .in1(Extend), .in2(Mem_Data), .in3({{8{1'b0}}, PC_1}), .out(multiplexer_3_out),
    .sel(Write1));
  SignExt signext_1 (.Imm(Imm), .SignExt(S_Ext), .Output(Extend));
  not not_1 (not_1_out, Halt);
  Register u_PC (.D(multiplexer_2_out), .en(Halt), .Q(PC_q), .clk(Clk));  // open: clr
  LED u_Halt (.in(not_1_out));
  Adder adder_2 (.a(PC_q), .b(8'h1), .out(PC_1));  // open: cin, cout
  RegFile regfile_1 (
    .Read_Register1(Rs), .Write_Register1(Rs), .Write_Data2(Upper_Bits), .Read_Data1(R_Data1),
    .Read_Data2(regfile_1_read_data2), .Clock(Clk), .Write_Register2(Rs_1), .Write_Data1(multiplexer_3_out),
    .Read_Register2(Imm[7:5]), .writeEnable2(W_En2), .writeEnable1(W_En1));
  ROM #(.dataWidth(16)) rom_1 (.addr(PC_q), .data({OpCode, Rs, Imm, SubOp}), .sel(1'b1));
  Register #(.width(16)) register_1 (.D(R_Data1), .en(Put), .Q(register_1_q), .clk(Clk));  // open: clr
  ALU alu_1 (
    .A(multiplexer_4_out), .B(multiplexer_5_out), .ALU_Op(ALU), .ALU_result(ALU_Result),
    .Mul_Div_Upper(Upper_Bits));
  Multiplexer #(.width(16), .enable("false")) multiplexer_4 (
    .in0(R_Data1), .in1(regfile_1_read_data2), .out(multiplexer_4_out), .sel(ALU_A));
  Multiplexer #(.select(2), .width(16), .enable("false")) multiplexer_5 (
    .in0(regfile_1_read_data2), .in1(Extend), .in2({16{1'b0}}), .in3(16'hff), .out(multiplexer_5_out),
    .sel(ALU_B));
  Hex_Digit_Display hex_digit_display_1 (.value(register_1_q[15:12]));  // open: dp
  Hex_Digit_Display hex_digit_display_2 (.value(register_1_q[11:8]));  // open: dp
  Hex_Digit_Display hex_digit_display_3 (.value(register_1_q[3:0]));  // open: dp
  Hex_Digit_Display hex_digit_display_4 (.value(register_1_q[7:4]));  // open: dp
  Clock clock_1 (.out(Clk));
  RAM #(.dataWidth(16), .bus("separate")) ram_1 (
    .addr(ALU_Result[7:0]), .din(R_Data1), .data(Mem_Data), .str(MemWrite), .sel(1'b1), .clk(Clk),
    .ld(MemRead));  // open: clr
  Control control_1 (
    .OpCode(OpCode), .SubOp(SubOp), .Write_Enable1(W_En1), .Write_Enable2(W_En2), .MemWrite(MemWrite),
    .MemRead(MemRead), .Halt(Halt), .Put(Put), .ALU(ALU), .ALU_A(ALU_A), .ALU_B(ALU_B), .PC(PC),
    .Write_Data1(Write1), .Sign_Extend(S_Ext));

  // Other names for the same wires on the sheet: Rt[2:0] = Imm[7:5]

  // Notes on the sheet:
  //   Katie Pucci, kev19@pitt.edu
  //   Instruction memory
  //   contents of rom_1 (hex, n*v repeats v):
  //   8004 b000 821a b200 200 b200 8414 b400 401 b400 17f0 b600 17f1 b800 8a04 ba00 4740 b600 8c06 bc00
  //   4981 b800 b001
  //   Data Memory
endmodule

module RegFile (
  input  [2:0] Read_Register1,
  input  [15:0] Write_Data1,
  input  [15:0] Write_Data2,
  input  [2:0] Read_Register2,
  input  Clock,
  input  writeEnable1,
  input  [2:0] Write_Register1,
  input  writeEnable2,
  input  [2:0] Write_Register2,
  output [15:0] Read_Data1,
  output [15:0] Read_Data2
);

  wire demultiplexer_3_out0, demultiplexer_3_out1, demultiplexer_3_out2, demultiplexer_3_out3,
       demultiplexer_3_out4, demultiplexer_3_out5, demultiplexer_3_out6, demultiplexer_3_out7,
       demultiplexer_4_out0, demultiplexer_4_out1, demultiplexer_4_out2, demultiplexer_4_out3,
       demultiplexer_4_out4, demultiplexer_4_out5, demultiplexer_4_out6, demultiplexer_4_out7, En_Reg000,
       En_Reg001, En_Reg010, En_Reg011, En_Reg100, En_Reg101, En_Reg110, En_Reg111;
  wire [15:0] Data_Reg000, Data_Reg001, Data_Reg010, Data_Reg011, Data_Reg100, Data_Reg101, Data_Reg110,
       Data_Reg111, demultiplexer_1_out0, demultiplexer_1_out1, demultiplexer_1_out2, demultiplexer_1_out3,
       demultiplexer_1_out4, demultiplexer_1_out5, demultiplexer_1_out6, demultiplexer_1_out7,
       demultiplexer_2_out0, demultiplexer_2_out1, demultiplexer_2_out2, demultiplexer_2_out3,
       demultiplexer_2_out4, demultiplexer_2_out5, demultiplexer_2_out6, demultiplexer_2_out7, Reg000_q,
       Reg001_q, Reg010_q, Reg011_q, Reg100_q, Reg101_q, Reg110_q, Reg111_q;

  Demultiplexer #(.select(3), .width(16), .enable("false")) demultiplexer_1 (
    .out0(demultiplexer_1_out0), .out1(demultiplexer_1_out1), .out2(demultiplexer_1_out2),
    .out3(demultiplexer_1_out3), .out4(demultiplexer_1_out4), .out5(demultiplexer_1_out5),
    .out6(demultiplexer_1_out6), .out7(demultiplexer_1_out7), .in(Write_Data1), .sel(Write_Register1));
  Demultiplexer #(.select(3), .width(16), .enable("false")) demultiplexer_2 (
    .out0(demultiplexer_2_out0), .out1(demultiplexer_2_out1), .out2(demultiplexer_2_out2),
    .out3(demultiplexer_2_out3), .out4(demultiplexer_2_out4), .out5(demultiplexer_2_out5),
    .out6(demultiplexer_2_out6), .out7(demultiplexer_2_out7), .in(Write_Data2), .sel(Write_Register2));
  Demultiplexer #(.select(3), .enable("false")) demultiplexer_3 (
    .out0(demultiplexer_3_out0), .out1(demultiplexer_3_out1), .out2(demultiplexer_3_out2),
    .out3(demultiplexer_3_out3), .out4(demultiplexer_3_out4), .out5(demultiplexer_3_out5),
    .out6(demultiplexer_3_out6), .out7(demultiplexer_3_out7), .in(writeEnable1), .sel(Write_Register1));
  Demultiplexer #(.select(3), .enable("false")) demultiplexer_4 (
    .out0(demultiplexer_4_out0), .out1(demultiplexer_4_out1), .out2(demultiplexer_4_out2),
    .out3(demultiplexer_4_out3), .out4(demultiplexer_4_out4), .out5(demultiplexer_4_out5),
    .out6(demultiplexer_4_out6), .out7(demultiplexer_4_out7), .in(writeEnable2), .sel(Write_Register2));
  assign Data_Reg000 = demultiplexer_1_out0 | demultiplexer_2_out0;  // OR_Gate or_1, 16 bits wide
  assign Data_Reg001 = demultiplexer_1_out1 | demultiplexer_2_out1;  // OR_Gate or_2, 16 bits wide
  assign Data_Reg010 = demultiplexer_1_out2 | demultiplexer_2_out2;  // OR_Gate or_3, 16 bits wide
  assign Data_Reg011 = demultiplexer_1_out3 | demultiplexer_2_out3;  // OR_Gate or_4, 16 bits wide
  assign Data_Reg100 = demultiplexer_1_out4 | demultiplexer_2_out4;  // OR_Gate or_5, 16 bits wide
  assign Data_Reg101 = demultiplexer_1_out5 | demultiplexer_2_out5;  // OR_Gate or_6, 16 bits wide
  assign Data_Reg110 = demultiplexer_1_out6 | demultiplexer_2_out6;  // OR_Gate or_7, 16 bits wide
  assign Data_Reg111 = demultiplexer_1_out7 | demultiplexer_2_out7;  // OR_Gate or_8, 16 bits wide
  or or_9 (En_Reg000, demultiplexer_3_out0, demultiplexer_4_out0);
  or or_10 (En_Reg001, demultiplexer_3_out1, demultiplexer_4_out1);
  or or_11 (En_Reg010, demultiplexer_3_out2, demultiplexer_4_out2);
  or or_12 (En_Reg011, demultiplexer_3_out3, demultiplexer_4_out3);
  or or_13 (En_Reg100, demultiplexer_3_out4, demultiplexer_4_out4);
  or or_14 (En_Reg101, demultiplexer_3_out5, demultiplexer_4_out5);
  or or_15 (En_Reg110, demultiplexer_3_out6, demultiplexer_4_out6);
  or or_16 (En_Reg111, demultiplexer_3_out7, demultiplexer_4_out7);
  Register #(.width(16)) Reg000 (.D(Data_Reg000), .en(En_Reg000), .Q(Reg000_q), .clk(Clock));  // open: clr
  Register #(.width(16)) Reg001 (.D(Data_Reg001), .en(En_Reg001), .Q(Reg001_q), .clk(Clock));  // open: clr
  Register #(.width(16)) Reg010 (.D(Data_Reg010), .en(En_Reg010), .Q(Reg010_q), .clk(Clock));  // open: clr
  Register #(.width(16)) Reg011 (.D(Data_Reg011), .en(En_Reg011), .Q(Reg011_q), .clk(Clock));  // open: clr
  Register #(.width(16)) Reg100 (.D(Data_Reg100), .en(En_Reg100), .Q(Reg100_q), .clk(Clock));  // open: clr
  Register #(.width(16)) Reg101 (.D(Data_Reg101), .en(En_Reg101), .Q(Reg101_q), .clk(Clock));  // open: clr
  Register #(.width(16)) Reg110 (.D(Data_Reg110), .en(En_Reg110), .Q(Reg110_q), .clk(Clock));  // open: clr
  Register #(.width(16)) Reg111 (.D(Data_Reg111), .en(En_Reg111), .Q(Reg111_q), .clk(Clock));  // open: clr
  Multiplexer #(.select(3), .width(16), .enable("false")) multiplexer_1 (
    .in0(Reg000_q), .in1(Reg001_q), .in2(Reg010_q), .in3(Reg011_q), .in4(Reg100_q), .in5(Reg101_q),
    .in6(Reg110_q), .in7(Reg111_q), .out(Read_Data1), .sel(Read_Register1));
  Multiplexer #(.select(3), .width(16), .enable("false")) multiplexer_2 (
    .in0(Reg000_q), .in1(Reg001_q), .in2(Reg010_q), .in3(Reg011_q), .in4(Reg100_q), .in5(Reg101_q),
    .in6(Reg110_q), .in7(Reg111_q), .out(Read_Data2), .sel(Read_Register2));

  // Other names for the same wires on the sheet: W_En1 = writeEnable1; W_En2 = writeEnable2;
  //   WriteReg1[2:0] = Write_Register1; WriteReg2[2:0] = Write_Register2
endmodule

module ALU (
  input  [15:0] A,
  input  [3:0] ALU_Op,
  input  [15:0] B,
  output [15:0] Mul_Div_Upper,
  output [15:0] ALU_result
);

  wire [0:0] comparator_1_eq, comparator_1_gt, comparator_1_lt, not_1_out;
  wire [15:0] adder_1_out, and_1_out, Div_Upper, divider_1_out, Mul_Upper, multiplier_1_out, nor_1_out,
       shifter_1_out, shifter_2_out, subtractor_1_out;

  assign and_1_out = A & B;  // AND_Gate and_1, 16 bits wide
  assign nor_1_out = ~(A | B);  // NOR_Gate nor_1, 16 bits wide
  Adder #(.width(16)) adder_1 (.a(A), .b(B), .out(adder_1_out));  // open: cin, cout
  Subtractor #(.width(16)) subtractor_1 (.a(A), .b(B), .out(subtractor_1_out));  // open: bin, bout
  Divider #(.width(16)) divider_1 (.a(A), .b(B), .out(divider_1_out), .rem(Div_Upper));  // open: upper
  Multiplier #(.width(16)) multiplier_1 (.a(A), .b(B), .out(multiplier_1_out), .cout(Mul_Upper));  // open: cin
  Shifter #(.width(16)) shifter_1 (.in(A), .\dist (B[3:0]), .out(shifter_1_out));
  Shifter #(.width(16), .shift("lr")) shifter_2 (.in(A), .\dist (B[3:0]), .out(shifter_2_out));
  Comparator #(.width(16)) comparator_1 (
    .a(A), .b({16{1'b0}}), .gt(comparator_1_gt[0]), .eq(comparator_1_eq[0]), .lt(comparator_1_lt[0]));
  not not_1 (not_1_out[0], comparator_1_eq[0]);
  Multiplexer #(.select(4), .width(16), .enable("false")) multiplexer_1 (
    .in0(and_1_out), .in1(nor_1_out), .in2(adder_1_out), .in3(adder_1_out), .in4(adder_1_out),
    .in5(subtractor_1_out), .in6(divider_1_out), .in7(multiplier_1_out), .in8(shifter_1_out),
    .in9(shifter_2_out), .in10({{15{1'b0}}, not_1_out[0]}), .in11({{15{1'b0}}, comparator_1_eq[0]}),
    .in12({{15{1'b0}}, comparator_1_gt[0]}), .in13({{15{1'b0}}, comparator_1_lt[0]}), .in14(and_1_out),
    .in15(and_1_out), .out(ALU_result), .sel(ALU_Op));
  Multiplexer #(.width(16), .enable("false")) multiplexer_2 (
    .in0(Div_Upper), .in1(Mul_Upper), .out(Mul_Div_Upper), .sel(ALU_Op[0]));
endmodule

module Control (
  input  [3:0] OpCode,
  input  SubOp,
  output Write_Enable1,
  output Write_Enable2,
  output MemWrite,
  output MemRead,
  output Halt,
  output Put,
  output [3:0] ALU,
  output ALU_A,
  output [1:0] ALU_B,
  output [1:0] PC,
  output [1:0] Write_Data1,
  output Sign_Extend
);

  wire and_1_out, and_2_out, and_3_out, and_4_out, and_6_out, and_8_out, and_9_out, and_10_out, and_13_out,
       and_14_out, and_15_out, and_16_out, and_17_out, and_18_out, and_19_out, and_20_out, and_21_out,
       and_22_out, and_23_out, and_27_out, and_30_out, and_31_out, and_32_out, and_33_out, not_1_out,
       not_2_out, not_3_out, not_4_out, not_5_out, not_6_out, not_7_out, not_8_out, not_9_out, not_10_out,
       not_11_out, not_12_out, or_1_out, or_2_out, or_3_out, xnor_1_out, xor_1_out;

  and and_1 (and_1_out, OpCode[3], OpCode[1]);
  and and_2 (and_2_out, OpCode[0], SubOp);
  and and_3 (and_3_out, OpCode[3], OpCode[1]);
  and and_4 (and_4_out, OpCode[0], not_1_out);
  not not_1 (not_1_out, SubOp);
  not not_2 (not_2_out, OpCode[3]);
  not not_3 (not_3_out, OpCode[3]);
  nand nand_1 (Halt, and_1_out, and_2_out);
  and and_5 (Put, and_3_out, and_4_out);
  and and_6 (and_6_out, not_2_out, OpCode[2]);
  and and_7 (ALU_A, and_6_out, and_8_out);
  and and_8 (and_8_out, OpCode[1], OpCode[0]);
  and and_9 (and_9_out, not_3_out, OpCode[2]);
  and and_10 (and_10_out, not_3_out, OpCode[0]);
  or or_1 (or_1_out, OpCode[1], OpCode[0]);
  xnor xnor_1 (xnor_1_out, OpCode[2], OpCode[1]);
  and and_11 (ALU_B[1], and_9_out, or_1_out);
  and and_12 (ALU_B[0], and_10_out, xnor_1_out);
  not not_4 (not_4_out, OpCode[3]);
  not not_5 (not_5_out, OpCode[2]);
  not not_6 (not_6_out, OpCode[1]);
  not not_7 (not_7_out, OpCode[0]);
  not not_8 (not_8_out, SubOp);
  not not_9 (not_9_out, OpCode[3]);
  and and_13 (and_13_out, not_9_out, not_10_out);
  not not_10 (not_10_out, OpCode[2]);
  and and_14 (and_14_out, OpCode[1], OpCode[0]);
  and and_15 (and_15_out, OpCode[2], OpCode[1]);
  and and_16 (and_16_out, OpCode[0], not_11_out);
  not not_11 (not_11_out, SubOp);
  and and_17 (and_17_out, OpCode[0], SubOp);
  and and_18 (and_18_out, not_4_out, not_5_out);
  or or_2 (or_2_out, and_18_out, and_19_out);
  and and_19 (and_19_out, not_6_out, not_7_out);
  and and_20 (and_20_out, not_5_out, not_6_out);
  and and_21 (and_21_out, and_20_out, not_8_out);
  and and_22 (and_22_out, not_4_out, OpCode[1]);
  and and_23 (and_23_out, and_22_out, OpCode[0]);
  and and_24 (Write_Enable2, and_13_out, and_14_out);
  and and_25 (MemRead, and_15_out, and_16_out);
  and and_26 (MemWrite, and_15_out, and_17_out);
  nor nor_1 (Sign_Extend, OpCode[3], SubOp);
  or or_3 (or_3_out, or_2_out, and_21_out);
  and and_27 (and_27_out, and_23_out, not_8_out);
  or or_4 (Write_Enable1, or_3_out, and_27_out);
  xor xor_1 (xor_1_out, OpCode[1], OpCode[0]);
  and and_28 (Write_Data1[1], OpCode[2], OpCode[1]);
  and and_29 (PC[1], OpCode[3], xor_1_out);
  and and_30 (and_30_out, OpCode[2], xor_1_out);
  and and_31 (and_31_out, OpCode[3], not_12_out);
  not not_12 (not_12_out, OpCode[1]);
  and and_32 (and_32_out, OpCode[0], SubOp);
  and and_33 (and_33_out, and_31_out, and_32_out);
  or or_5 (PC[0], and_30_out, and_33_out);

  assign ALU = {OpCode[2:0], SubOp};
  assign Write_Data1[0] = OpCode[3];

  // Other names for the same wires on the sheet: Opcode_0 = OpCode[0]; Opcode_1 = OpCode[1]; Opcode_2 = OpCode[2];
  //   S_Ext = Sign_Extend; W_En1 = Write_Enable1; W_En2 = Write_Enable2; Opcode_3 = OpCode[3];
  //   Write1[1:0] = {Write_Data1[1], OpCode[3]}

  // Notes on the sheet:
  //   Inputs
  //   Halt
  //   Put
  //   ALU_A
  //   ALU_B
  //   Write_Enable1
  //   Write_Enable2
  //   MemWrite/MemRead
  //   ALU
  //   Sign_Extend
  //   PC
  //   Write_Data1
  //   Outputs
endmodule

module SignExt (
  input  [7:0] Imm,
  input  SignExt,
  output [15:0] Output
);

  wire multiplexer_1_out;

  Multiplexer #(.enable("false")) multiplexer_1 (.in0(1'b0), .in1(Imm[7]), .out(multiplexer_1_out), .sel(SignExt));
  assign Output = {{8{multiplexer_1_out}}, Imm};  // Bit_Extender bit_extender_1
endmodule
