// Logisim project project2_register_file_example.circ as structural Verilog: 1 circuit, main circuit main
module main (
  input  [7:0] WritePort1,
  input  [7:0] WritePort2,
  input  WriteEnable1,
  input  WriteEnable2,
  input  [1:0] ReadReg,
  input  Clock,
  output [7:0] Output
);

  wire demultiplexer_1_out0, demultiplexer_1_out1, demultiplexer_1_out2, demultiplexer_1_out3,
       demultiplexer_2_out0, demultiplexer_2_out1, demultiplexer_2_out2, demultiplexer_2_out3, EnableReg0,
       EnableReg1, EnableReg2, EnableReg3;
  wire [1:0] WriteReg2;
  wire [7:0] DataReg0, DataReg1, DataReg2, DataReg3, demultiplexer_3_out0, demultiplexer_3_out1,
       demultiplexer_3_out2, demultiplexer_3_out3, demultiplexer_4_out0, demultiplexer_4_out1,
       demultiplexer_4_out2, demultiplexer_4_out3, register_1_q, register_2_q, register_3_q, register_4_q;

  Demultiplexer #(.select(2), .enable("false")) demultiplexer_1 (
    .out0(demultiplexer_1_out0), .out1(demultiplexer_1_out1), .out2(demultiplexer_1_out2),
    .out3(demultiplexer_1_out3), .in(WriteEnable1), .sel(ReadReg));
  Demultiplexer #(.select(2), .enable("false")) demultiplexer_2 (
    .out0(demultiplexer_2_out0), .out1(demultiplexer_2_out1), .out2(demultiplexer_2_out2),
    .out3(demultiplexer_2_out3), .in(WriteEnable2), .sel(WriteReg2));
  Demultiplexer #(.select(2), .width(8), .enable("false")) demultiplexer_3 (
    .out0(demultiplexer_3_out0), .out1(demultiplexer_3_out1), .out2(demultiplexer_3_out2),
    .out3(demultiplexer_3_out3), .in(WritePort1), .sel(ReadReg));
  Demultiplexer #(.select(2), .width(8), .enable("false")) demultiplexer_4 (
    .out0(demultiplexer_4_out0), .out1(demultiplexer_4_out1), .out2(demultiplexer_4_out2),
    .out3(demultiplexer_4_out3), .in(WritePort2), .sel(WriteReg2));
  assign DataReg0 = demultiplexer_3_out0 | demultiplexer_4_out0;  // OR_Gate or_1, 8 bits wide
  assign DataReg1 = demultiplexer_3_out1 | demultiplexer_4_out1;  // OR_Gate or_2, 8 bits wide
  assign DataReg2 = demultiplexer_3_out2 | demultiplexer_4_out2;  // OR_Gate or_3, 8 bits wide
  assign DataReg3 = demultiplexer_3_out3 | demultiplexer_4_out3;  // OR_Gate or_4, 8 bits wide
  or or_5 (EnableReg0, demultiplexer_1_out0, demultiplexer_2_out0);
  or or_6 (EnableReg1, demultiplexer_1_out1, demultiplexer_2_out1);
  or or_7 (EnableReg2, demultiplexer_1_out2, demultiplexer_2_out2);
  or or_8 (EnableReg3, demultiplexer_1_out3, demultiplexer_2_out3);
  Register register_1 (.D(DataReg0), .en(EnableReg0), .Q(register_1_q), .clk(Clock));  // open: clr
  Register register_2 (.D(DataReg1), .en(EnableReg1), .Q(register_2_q), .clk(Clock));  // open: clr
  Register register_3 (.D(DataReg2), .en(EnableReg2), .Q(register_3_q), .clk(Clock));  // open: clr
  Register register_4 (.D(DataReg3), .en(EnableReg3), .Q(register_4_q), .clk(Clock));  // open: clr
  Multiplexer #(.select(2), .width(8), .enable("false")) multiplexer_1 (
    .in0(register_1_q), .in1(register_2_q), .in2(register_3_q), .in3(register_4_q), .out(Output),
    .sel(ReadReg));
  Adder #(.width(2)) adder_1 (.a(2'b01), .b(ReadReg), .out(WriteReg2));  // open: cin, cout

  // Other names for the same wires on the sheet: WriteReg1[1:0] = ReadReg

  // Notes on the sheet:
  //   The second Write Register is the Read Register + 1
  //   Write Register is the same as the Read Register
endmodule
